# Fritzing sketch Távirányító (saved by Fritzing 0.9.4)
breadboards: 1

parts:
  Nano = Arduino Nano (Rev3.0)
  MPU6050 = InvenSense MPU6050
  nRF24L01 = NRF24L01+ Breakout Board
  LED1 = LED - 5mm [color="Blue (525nm)" package="5 mm [THT]"]
  R1 = Resistor [tolerance=±5% resistance=220 package=THT]
  R2 = Resistor [tolerance=±5% resistance=10k package=THT]
  VCC = DC Power [voltage=6.5V]
  S1 = Square Pushbutton

nets (from the schematic view):
  GND: Nano.GND, MPU6050.GND, nRF24L01.GND, LED1.cathode, R2.Pin_1, VCC.V-
  N1: Nano.D4, R2.Pin_0, S1.leg1
  N2: Nano.D5, R1.Pin_0
  N3: Nano.D7, nRF24L01.CS
  N4: Nano.D8, nRF24L01.CE
  N5: Nano.D10, MPU6050.INT
  N6: Nano.D11/MOSI, nRF24L01.MOSI
  N7: Nano.D12/MISO, nRF24L01.MISO
  N8: Nano.VIN, VCC.V+
  5V: Nano.5V, MPU6050.VCC, S1.leg0
  N9: Nano.A5, MPU6050.SCL
  N10: Nano.A4, MPU6050.SDA
  3V3: Nano.3V3, nRF24L01.VCC
  N11: Nano.D13/SCK, nRF24L01.SCK
  N12: LED1.anode, R1.Pin_1
