# Fritzing sketch kocsi (saved by Fritzing 0.9.4)
breadboards: 1

parts:
  Part1 = Arduino Uno (Rev3)
  Part2 = NRF24L01+ Breakout Board
  HC-SR04_Sensor_1 = HC-SR04 Ultrasonic Distance Sensor
  HC-SR04_Sensor_2 = HC-SR04 Ultrasonic Distance Sensor
  IC1 = L293D [package=THT]
  J1 = Basic Servo
  M1 = DC Motor
  piezo = Piezo Speaker
  100uf = Capacitor Polarized [package=cpol-radial-100uf-25v]
  VCC1 = DC Power [voltage=6.5V]
  VCC2 = Battery block 9V

nets:
  N1: Part1.D8, Part2.CS
  N2: Part1.D9_PWM, HC-SR04_Sensor_2.TRIG
  N3: Part1.D10_PWM/SS, J1.pulse
  N4: Part1.D11_PWM/MOSI, Part2.MOSI
  N5: Part1.D12/MISO, Part2.MISO
  N6: Part1.D13/SCK, Part2.SCK
  GND: Part1.GND, Part2.GND, HC-SR04_Sensor_1.ECHO, HC-SR04_Sensor_2.ECHO, IC1.0V, J1.gnd, piezo.pin2, 100uf.-, VCC1.V-, VCC2.-
  N7: Part1.D0/RX, HC-SR04_Sensor_1.GND
  N8: Part1.D1/TX, HC-SR04_Sensor_1.TRIG
  N9: Part1.D2, HC-SR04_Sensor_2.GND
  N10: Part1.D3_PWM, IC1.In_1
  N11: Part1.D4, IC1.In_2
  N12: Part1.D5_PWM, IC1.Enable_1
  N13: Part1.D6_PWM, piezo.pin1
  N14: Part1.D7, Part2.CE
  3V3: Part1.3V3, Part2.VCC
  VCC: Part1.5V, HC-SR04_Sensor_1.VCC, HC-SR04_Sensor_2.VCC, IC1.+V, J1.vcc, 100uf.+
  N15: Part1.VIN, VCC1.V+
  N16: IC1.Out_1_(_Controlled_by_Enable_1_), M1.pin_2
  N17: IC1.Out_2_(_Controlled_by_Enable_1_), M1.pin_1
  N18: IC1.+Vmotor, VCC2.+
