# Fritzing sketch ÚjKözpont (saved by Fritzing 0.9.4)
breadboards: 1

parts:
  Part1 = Arduino Uno (Rev3)
  Part2 = Arduino Nano (Rev3.0)
  Part3 = NRF24L01+ Breakout Board
  J1 = Piezo Speaker
  IC1 = L293D [package=THT]
  HC-SR04_Sensor_1 = HC-SR04 Ultrasonic Distance Sensor
  HC-SR04_Sensor_2 = HC-SR04 Ultrasonic Distance Sensor
  D1 = Rectifier Diode [part_number=1N4001 package="300 mil [THT]"]
  D2 = Rectifier Diode [part_number=1N4001 package="300 mil [THT]"]
  100uF = Capacitor Polarized [package=cpol-radial-100uf-25v]
  J2 = Basic Servo
  M1 = DC Motor
  VCC = Battery block 9V
  Vin = DC Power [voltage=6V]

nets (from the schematic view):
  N1: Part1.A4/SDA, Part2.A4
  N2: Part1.A5/SCL, Part2.A5
  N3: Part1.D4, HC-SR04_Sensor_1.GND
  N4: Part1.D5_PWM, HC-SR04_Sensor_1.TRIG
  N5: Part1.D6_PWM, HC-SR04_Sensor_2.GND
  N6: Part1.D7, HC-SR04_Sensor_2.TRIG
  VCC: Part1.5V, HC-SR04_Sensor_1.VCC, HC-SR04_Sensor_2.VCC
  GND: Part1.GND, Part2.GND, Part3.GND, J1.pin1, IC1.0V, HC-SR04_Sensor_1.ECHO, HC-SR04_Sensor_2.ECHO, 100uF.-, J2.gnd, VCC.-, Vin.V-
  N7: Part1.VIN, D1.cathode
  N8: Part2.D3, IC1.In_1
  N9: Part2.D4, IC1.In_2
  N10: Part2.D5, J2.pulse
  N11: Part2.D6, IC1.Enable_1
  N12: Part2.D7, Part3.CE
  N13: Part2.D8, Part3.CS
  N14: Part2.D9, J1.pin2
  N15: Part2.D11/MOSI, Part3.MOSI
  N16: Part2.D12/MISO, Part3.MISO
  N17: Part2.VIN, D2.cathode
  5V: Part2.5V, IC1.+V, 100uF.+, J2.vcc
  3V3: Part2.3V3, Part3.VCC
  N18: Part2.D13/SCK, Part3.SCK
  N19: IC1.Out_2_(_Controlled_by_Enable_1_), M1.pin_2
  N20: IC1.+Vmotor, VCC.+
  N21: D1.anode, D2.anode, Vin.V+

// code stored in the sketch: KpLokator.ino
/*
 Name:		LOKATOR (KICSIKOCSI KOZPONTI EGYSEG)
					Arduino WiFi Rev2
 Created:	1/9/2021 11:06:05 PM
 Author:	qbz
*/

#include <Wire.h>
#include "Lokator.h"

// Arduino WiFi Rev2 pin kiosztas
#define HC1Echo 4				// Elso HC-SR04-4P Echo
#define HC1Trig 5				// Elso HC-SR04-4P Triger
#define HC2Echo 6				// Hatso HC-SR04 Echo
#define HC2Trig 7				// Hatso HC-SR04 Triger

// egyeb allandok
#define LOKATOROK_SZAMA 2										// A kocsin mukodo lokatorok szama
#define FOGADOTT_TOMB_MERET 3								// A masik arduinotol fogadott adatok merete

byte kuldottAdatok[LOKATOROK_SZAMA];
byte fogadottAdatok[FOGADOTT_TOMB_MERET];
bool adatFogadasRendben = false;
Lokator elso(HC1Trig, HC1Echo);
Lokator hatso(HC2Trig, HC2Echo);

// debug
unsigned long currentTime;
unsigned long previousTime;
int L;

void adatokFogadasa(int n) {
	if (n != FOGADOTT_TOMB_MERET) digitalWrite(LED_BUILTIN, HIGH);
	else {
		digitalWrite(LED_BUILTIN, LOW);
		int i = 0;
		while (i < FOGADOTT_TOMB_MERET && Wire.available()) {
			fogadottAdatok[i] = Wire.read();
			i++;
		}
	}
}

void adatokKuldese() {
	kuldottAdatok[0] = elso.getTavolsag();
	kuldottAdatok[1] = hatso.getTavolsag();
	Wire.write(kuldottAdatok, sizeof(kuldottAdatok));
}

void setup() {
	pinMode(HC1Trig, OUTPUT);
	pinMode(HC1Echo, INPUT);
	pinMode(HC2Trig, OUTPUT);
	pinMode(HC2Echo, INPUT);
	pinMode(LED_BUILTIN, OUTPUT);
	Serial.begin(9600);
	Wire.begin(0x02);
	Wire.onReceive(adatokFogadasa);
	Wire.onRequest(adatokKuldese);
}

void loop() {

// debug
	currentTime = millis();
	L = currentTime - previousTime;
	previousTime = currentTime;
}

// code stored in the sketch: KpMotor.ino
/*
  Name:		MOTOR (KICSIKOCSI KOZPONTI EGYSEG)
					Arduino Nano
  Created:	1/9/2021 7:59:35 PM
  Author:	qbz
*/

#include <SPI.h>
#include <RF24_config.h>
#include <RF24.h>
#include <printf.h>
#include <nRF24L01.h>
#include <Wire.h>
#include <Servo.h>


// Arduino Nano pin kiosztas
#define MOTOR_ELORE 3								// L293 "Input 1" (elore forog a motor)
#define MOTOR_HATRA 4								// L293 "Input 2" (hatra forog a motor)
#define SERVO 5											// A szervo motor vezerloje
#define MOTOR_ENABLE 6							// L293 "Enable" (motor bekapcsolasa)
#define RF_CE 7											// nRF24L01 "Chip Enable"
#define RF_CS 8											// nRF24L01 "Chip Set"
#define PIEZZO 9										// csipogo
#define RF_MOSI 11									// nRF24L01 MOSI (Az ICSP kommunikaciohoz szukseges)
#define RF_MISO 12									// nRF24L01 MISO (Az ICSP kommunikaciohoz szukseges)
#define RF_SCK 13										// nRF24L01 SCK (Az ICSP kommunikaciohoz szukseges)

// egyeb allandok
#define TIMEOUT 100									// riasztas, ha ennyi cikluson át nem uzen a taviranyito
#define AKADALY 10									// ennel kozelebb (centimeterben)
#define MIN_SEBESSEG 100						// limit alatti erteknel nem indul a motor


RF24 radio(RF_CE, RF_CS);						// Radio letrehozasa
Servo kormany;											// Kormany letrehozasa

byte kontrollerSebesseg;						// A taviranyito altal kuldott sebesseg adat
byte kontrollerKormany;							// A taviranyito altal kuldott kormanyzas adat
bool kontrollerGomb;								// A taviranyito gombjanak allapota
int kontrollerOfflineTimer;					// A taviranyito offline allapotanak kesleltetese
bool kontrollerOnline;							// A taviranyito online allapota
byte elsoLokator;										// Az elso lokator altal mert tavolsag
byte hatsoLokator;									// A hatso lokator altal mert tavolsag

void mozgas()
{
	lokatorOlvasasa();
	kontrollerOlvasasa();
	kormany.write(kontrollerKormany);
	analogWrite(MOTOR_ENABLE, sebessegSzamitasa());
}

void lokatorOlvasasa()
{
	Wire.requestFrom(0x02, 2);
	if (Wire.available()) {
		elsoLokator = Wire.read();
		hatsoLokator = Wire.read();
	}
}

void kontrollerOlvasasa()
{
	radio.startListening();
	if (radio.available()) radioAdatokFeldolgozasa();
	else kontrollerOfflineTimer++;
	if (kontrollerOfflineTimer == TIMEOUT) nincsKapcsolat();
}

void radioAdatokFeldolgozasa()
{
	if (!kontrollerOnline) lettKapcsolat();
	byte csomag[3];
	radio.read(&csomag, sizeof(csomag));
	kontrollerOfflineTimer = 0;
	kontrollerSebesseg = csomag[0];
	kontrollerKormany = csomag[1];
	kontrollerGomb = csomag[2];
}

void nincsKapcsolat()
{
	tone(PIEZZO, 1000, 40);
	delay(100);
	tone(PIEZZO, 880, 20);
	delay(100);
	tone(PIEZZO, 880, 20);
	kontrollerOnline = false;
	kontrollerOfflineTimer = 0;
}

void lettKapcsolat()
{
	tone(PIEZZO, 880, 40);
	delay(250);
	tone(PIEZZO, 1760, 40);
	kontrollerOnline = true;
}

int sebessegSzamitasa()
{
	if (kontrollerGomb == 1 && kontrollerOnline) {
		int sebesseg = map(kontrollerSebesseg, 0, 255, -255, 255);
		if (sebesseg < -MIN_SEBESSEG) {														// ha a sebesseg alapjan hatrament van es nagyobb a minimumnal
			digitalWrite(MOTOR_ELORE, LOW);
			digitalWrite(MOTOR_HATRA, HIGH);
			if (hatsoLokator < AKADALY) sebesseg = 0;								// ha a hatso lokotor alapjan kozel egy akadaly
			else sebesseg = -sebesseg;															// a negativ sebessegertek abszoluterteke
		}
		else if (sebesseg > MIN_SEBESSEG) {												// ha eloremenet van es a sebesseg meghaladja a minimumiot
			digitalWrite(MOTOR_ELORE, HIGH);
			digitalWrite(MOTOR_HATRA, LOW);
			if (elsoLokator < AKADALY) sebesseg = 0;								// ha az elso lokotor alapjan kozel egy akadaly
		}
		else sebesseg = 0;
		return sebesseg;
	}
	else return 0;
}

//void debug()
//{
//	Serial.print("K[0]: ");
//	Serial.print(kontrollerSebesseg);
//	Serial.print(" K[1]: ");
//	Serial.print(kontrollerKormany);
//	Serial.print(" K[2]: ");
//	Serial.print(kontrollerGomb);
//	Serial.print(" OTime: ");
//	Serial.print(kontrollerOfflineTimer);
//	Serial.print(" KOnline: ");
//	Serial.print(kontrollerOnline);
//	Serial.print(" ELok: ");
//	Serial.print(elsoLokator);
//	Serial.print(" HLok: ");
//	Serial.println(hatsoLokator);
//}

void setup()
{
	pinMode(MOTOR_ELORE, OUTPUT);
	pinMode(MOTOR_HATRA, OUTPUT);
	pinMode(MOTOR_ENABLE, OUTPUT);
	pinMode(PIEZZO, OUTPUT);
	Serial.begin(9600);
	Wire.begin();
	radio.begin();                          // Radio bekapcsolasa
	radio.openReadingPipe(0, 96);						// csatorna nyitasa adatok fogadasahoz a taviranyitotol
	radio.setPALevel(RF24_PA_MIN);					// Radio tererejenek minimumra allitasa
	kormany.attach(SERVO);									// Szervo csatlakoztatasa
	kormany.write(90);											// kormany kiegyenesitese
}

void loop()
{
	mozgas();
}
